# Fritzing sketch wiring2019 (saved by Fritzing 0.9.3b)

parts:
  Part1 = Arduino Mega ADK (Rev3)
  M1 = DC Motor  # not connected
  VCC1 = Battery  # not connected
  NEOPIXEL2 = Neopixel Strip -- White (30/m)
  TRELLIS1 = Adafruit Trellis

nets:
  N1: Part1.A3, TRELLIS1.INT
  N2: Part1.D21/SCL, TRELLIS1.SCL
  N3: Part1.D20/SDA, TRELLIS1.SDA
  GND: Part1.GND, NEOPIXEL2.GND, TRELLIS1.GND
  5V: Part1.5V, NEOPIXEL2.+5V, TRELLIS1.5V
  N4: Part1.D41, NEOPIXEL2.Din

notes:
  GND M+
  12V M-
  Victor
  PWM
  12V+ 12V-
  40A +
  -
  PDP
  + 5V -

custom parts:
  Neopixel Strip -- White (30/m): These NeoPixel strips have 30 digitally-addressable pixel LEDs per meter and are very affordable and are only 12.5 mm wide, 10 mm if you remove the strip from the casing.
